# Fritzing sketch Kiln (saved by Fritzing 0.9.3b)

parts:
  Composant1 = Arduino Uno (Rev3)
  U1 = MAX6675 [package=so08]
  S1 = H-Bridge with L298N
  M2 = DC Motor
  M3 = DC Motor

nets:
  N1: Composant1.D5_PWM, U1.MISO
  N2: Composant1.D6_PWM, U1.CS
  N3: Composant1.D7, U1.SCK
  5V: Composant1.5V, U1.VDD
  GND: Composant1.GND, U1.VSS
  N4: S1.M1-01, M3.pin_2
  N5: S1.M1-02, M3.pin_1
  N6: S1.M2-01, M2.pin_2
  N7: S1.M2-02, M2.pin_1

custom parts:
  H-Bridge with L298N: h-bridge
